# Fritzing sketch esquema (saved by Fritzing 0.9.3b)
breadboards: 1

parts:
  Componente1 = Arduino Uno (Rev3)
  T1 = LM35 Temperature Sensor [package="TO92 [THT]"]
  U1 = 7-SEGMENT-4DIGIT [package=7-segment-4digit]
  S1 = Momentary Switch [package=ksa_sealed_tac_switch]
  LED1 = smd LED [color="Yellow (595nm)" package="0603 [SMD]"]
  LED2 = smd LED [color="Red (633nm)" package="1206 [SMD]"]
  LED3 = smd LED [color="Blue (430nm)" package="1206 [SMD]"]
  R1 = Resistor [tolerance=±5% resistance=220 package="0402 [SMD]"]
  R2 = Resistor [tolerance=±5% resistance=220 package="0402 [SMD]"]
  R3 = Resistor [tolerance=±5% resistance=220 package="0402 [SMD]"]
  R4 = Resistor [tolerance=±5% resistance=220 package="0402 [SMD]"]
  R5 = Resistor [tolerance=±5% resistance=220 package="0402 [SMD]"]
  R6 = Resistor [tolerance=±5% resistance=220 package="0402 [SMD]"]
  hc-sr1 = hc-sr04

nets:
  N1: Componente1.A0, hc-sr1.Trig
  N2: Componente1.A1, hc-sr1.Echo
  N3: Componente1.A3, R3.Pin_0
  N4: Componente1.A4/SDA, R2.Pin_0
  N5: Componente1.A5/SCL, R1.Pin_0
  N6: Componente1.D8, U1.8
  N7: Componente1.D9_PWM, R6.Pin_0
  N8: Componente1.D10_PWM/SS, R5.Pin_0
  N9: Componente1.D11_PWM/MOSI, T1.GND
  N10: Componente1.D1/TX, S1.2, R4.Pin_1
  N11: Componente1.D4, U1.7
  N12: Componente1.D5_PWM, U1.5
  N13: Componente1.D6_PWM, U1.4
  N14: Componente1.D7, U1.11
  5V: Componente1.5V, hc-sr1.VCC
  GND: Componente1.GND, T1.+Vs, S1.4, LED1.cathode, LED2.cathode, LED3.cathode, R4.Pin_0, hc-sr1.GND
  N15: U1.13, R6.Pin_1
  N16: LED1.anode, R2.Pin_1
  N17: LED2.anode, R1.Pin_1
  N18: LED3.anode, R3.Pin_1
